// Digital circuit Assembly Workspace.dig as structural Verilog
module Assembly_Workspace (
  input  clk
);

  wire button_1_out, button_2_out, button_3_out, telescope_assembler_computer_1_p7,
       telescope_assembler_computer_1_p10, telescope_assembler_computer_1_p14,
       telescope_assembler_computer_1_p15, telescope_assembler_computer_1_p16,
       telescope_assembler_computer_1_p17, telescope_assembler_computer_1_p18,
       telescope_assembler_computer_1_p19, telescope_assembler_computer_1_p20,
       telescope_assembler_computer_1_p21, telescope_assembler_computer_1_p22;
  wire [6:0] Text_Input_d;
  wire [15:0] telescope_assembler_computer_1_p5, telescope_assembler_computer_1_p8,
       telescope_assembler_computer_1_p9, telescope_assembler_computer_1_p12,
       telescope_assembler_computer_1_p13;
  wire [31:0] telescope_assembler_computer_1_p11;

  Button button_1 (.out(button_1_out));
  Button button_2 (.out(button_2_out));
  Button button_3 (.out(button_3_out));
  ROM #(.AddrBits(24), .Bits(7)) Text_Input (
    .A(telescope_assembler_computer_1_p11[23:0]), .sel(1'b1), .D(Text_Input_d));
  // Telescope_Assembler_Computer telescope_assembler_computer_1: pin names not known; wires that end beside it: button_1_out, button_2_out, button_3_out, clk, telescope_assembler_computer_1_p5, Text_Input_d, telescope_assembler_computer_1_p7, telescope_assembler_computer_1_p8, telescope_assembler_computer_1_p9, telescope_assembler_computer_1_p10, telescope_assembler_computer_1_p11, telescope_assembler_computer_1_p12, telescope_assembler_computer_1_p13, telescope_assembler_computer_1_p14, telescope_assembler_computer_1_p15, telescope_assembler_computer_1_p16, telescope_assembler_computer_1_p17, telescope_assembler_computer_1_p18, telescope_assembler_computer_1_p19, telescope_assembler_computer_1_p20, telescope_assembler_computer_1_p21, telescope_assembler_computer_1_p22
  RAMDualPort #(.AddrBits(16), .Bits(16)) RAM (
    .A(telescope_assembler_computer_1_p8), .Din(telescope_assembler_computer_1_p9),
    .str(telescope_assembler_computer_1_p10), .C(clk), .ld(1'b1), .D(telescope_assembler_computer_1_p5));
  LED led_1 (.in(telescope_assembler_computer_1_p7));
  LED led_2 (.in(telescope_assembler_computer_1_p17));
  LED led_3 (.in(telescope_assembler_computer_1_p18));
  LED led_4 (.in(telescope_assembler_computer_1_p19));
  LED led_5 (.in(telescope_assembler_computer_1_p20));
  LED led_6 (.in(telescope_assembler_computer_1_p21));
  LED led_7 (.in(telescope_assembler_computer_1_p22));
  EEPROMDualPort #(.AddrBits(16), .Bits(16)) MC_Output (
    .A(telescope_assembler_computer_1_p12), .Din(telescope_assembler_computer_1_p13),
    .str(telescope_assembler_computer_1_p14), .C(clk), .ld(1'b0));  // open: D
  Terminal #(.termWidth(130), .termHeight(40)) File_As_Read (
    .D(telescope_assembler_computer_1_p15), .C(clk), .en(telescope_assembler_computer_1_p16));

  // Notes on the sheet:
  //   clk: Hz: 5000
  //   contents of Text_Input (hex, n*v repeats v):
  //   4a,4d,50,20,3e,4d,61,69,6e,a,a,5*25,a,20,20,51,75,69,63,6b,20
  //   ,74,65,73,74,20,74,6f,20,73,65,65,20,69,66,20,73,74,72,69,6e,67
  //   ,73,20,77,6f,72,6b,20,6f,72,20,6e,6f,74,a,20,20,4d,61,69,6e,20
  //   ,70,72,69,6e,74,73,20,6f,75,74,20,74,68,65,20,63,6f,6e,74,65,6e
  //   ,74,73,20,6f,66,20,4d,79,53,74,72,69,6e,67,20,74,6f,20,49,2f,4f
  //   ,a,5*25,a,a,23,4d,79,53,74,72,69,6e,67,20,3d,20,22,48,65,6c,6c
  //   ,6f,20,57,6f,72,6c,64,a,22,a,a,40,54,45,52,4d,46,4c,47,20,3d,20
  //   ,30,a,a,23,4d,61,69,6e,a,9,4c,44,49,20,46,4c,47,20,3e,54,45,52
  //   ,4d,46,4c,47,a,9,5a,52,4f,20,52,47,31,a,9,23,53,74,72,4c,6f,6f
  //   ,70,a,9,9,4c,4f,44,20,52,47,30,20,52,47,31,20,3e,4d,79,53,74,72
  //   ,69,6e,67,a,9,9,41,49,4e,20,41,44,44,20,52,47,30,20,31,3b,20,4a
  //   ,49,46,20,43,41,52,20,3e,53,74,72,44,6f,6e,65,a,9,9,4d,4f,56,20
  //   ,49,4f,20,52,47,30,a,9,9,49,4e,43,20,52,47,31,a,9,9,4a,4d,50,20
  //   ,3e,53,74,72,4c,6f,6f,70,a,9,23,53,74,72,44,6f,6e,65,a,9,48,4c
  //   ,54,a
  //   Assembler comes pre-installed on the computer. Just install some 16x16 RAM and you're good to go.
  //   Make sure MC Output is cleared (and make sure to press OK)
  //   contents of MC_Output (hex, n*v repeats v):
  //   4600,f,48,65,6c,6c,6f,20,57,6f,72,6c,64,a,ffff,50a0,0,b110,6001
  //   ,2,d901,4200,1b,3090,9911,4600,12
endmodule
