// Digital circuit TBOS Testing.dig as structural Verilog
module TBOS_Testing (
  input  clk,
  input  in_2
);

  wire button_1_out, button_2_out, button_3_out, or_1_out, telescope_computing_system_1_os_running;
  wire [15:0] Program_Files_d, Root_Drive_d, TBOS_2_0_d, telescope_computing_system_1_os_adr,
       telescope_computing_system_1_status_code;
  wire [16:0] keyboard_1_d;
  wire [18:0] telescope_computing_system_1_tk1_out;
  wire [19:0] telescope_computing_system_1_tnet_o_1, telescope_computing_system_1_tnet_o_2;
  wire [33:0] telescope_computing_system_1_d0_out, telescope_computing_system_1_d1_out;

  or or_1 (or_1_out, in_2, button_1_out);
  Button button_1 (.out(button_1_out));
  LED OS_Is_Running (.in(telescope_computing_system_1_os_running));
  // Probe Status on telescope_computing_system_1_status_code
  Telescope_Computing_System telescope_computing_system_1 (
    .OS_Running(telescope_computing_system_1_os_running),
    .Status_Code(telescope_computing_system_1_status_code), .Power_On(or_1_out), .Clock_Input(clk),
    .Pause(button_2_out), .Pause_Mode(1'b1), .STOP(button_3_out),
    .OS_Adr(telescope_computing_system_1_os_adr), .OS_In(TBOS_2_0_d), .D0_In(Root_Drive_d),
    .D0_Out(telescope_computing_system_1_d0_out), .D1_In(Program_Files_d),
    .D1_Out(telescope_computing_system_1_d1_out), .D2_In({16{1'b0}}), .D3_In({16{1'b0}}),
    .TNET_I_0({20{1'b0}}), .TNET_O_1(telescope_computing_system_1_tnet_o_1),
    .TNET_I_1(telescope_computing_system_1_tnet_o_1), .TNET_O_2(telescope_computing_system_1_tnet_o_2),
    .TNET_I_2(telescope_computing_system_1_tnet_o_2), .TNET_I_3({20{1'b0}}), .K0_In({17{1'b0}}),
    .TK1_Out(telescope_computing_system_1_tk1_out), .K1_In(keyboard_1_d), .K2_In({17{1'b0}}),
    .K3_In({17{1'b0}}), .GPI_0({18{1'b0}}), .GPI_1({18{1'b0}}), .GPI_2({18{1'b0}}), .GPI_3({18{1'b0}}));  // open: D2_Out, D3_Out, TNET_O_0, TNET_O_3, TK0_Out, TK2_Out, TK3_Out, GPO_0, GPO_1, GPO_2, GPO_3
  Button button_2 (.out(button_2_out));
  Button button_3 (.out(button_3_out));
  Keyboard keyboard_1 (
    .C(telescope_computing_system_1_tk1_out[18]), .en(telescope_computing_system_1_tk1_out[16]),
    .D(keyboard_1_d[15:0]), .av(keyboard_1_d[16]));
  // Probe OS Boot Drive Address on telescope_computing_system_1_os_adr
  ROM #(.AddrBits(16), .Bits(16)) TBOS_2_0 (.A(telescope_computing_system_1_os_adr), .sel(1'b1), .D(TBOS_2_0_d));
  Terminal terminal_1 (
    .D(telescope_computing_system_1_tk1_out[15:0]), .C(telescope_computing_system_1_tk1_out[18]),
    .en(telescope_computing_system_1_tk1_out[17]));
  EEPROMDualPort #(.AddrBits(16), .Bits(16)) Root_Drive (
    .A(telescope_computing_system_1_d0_out[31:16]), .Din(telescope_computing_system_1_d0_out[15:0]),
    .str(telescope_computing_system_1_d0_out[32]), .C(telescope_computing_system_1_d0_out[33]), .ld(1'b1),
    .D(Root_Drive_d));
  EEPROMDualPort #(.AddrBits(16), .Bits(16)) Program_Files (
    .A(telescope_computing_system_1_d1_out[31:16]), .Din(telescope_computing_system_1_d1_out[15:0]),
    .str(telescope_computing_system_1_d1_out[32]), .C(telescope_computing_system_1_d1_out[33]), .ld(1'b1),
    .D(Program_Files_d));

  // Notes on the sheet:
  //   clk: Hz: 256
  //   contents of TBOS_2_0 (hex, n*v repeats v):
  //   702,4600,20d,521*0,a654,a754,5000,1,50a0,f000,3090,50a0,e000,3090
  //   ,5010,702,5000,400,ae10,b912,5000,40,bb01,3078,b974,4600,345,50a0
  //   ,0,3078,b974,4600,564,d961,4a00,22f,5000,ff00,4600,240,3006,50a0
  //   ,4,3078,b974,4600,36e,5000,2,50a0,f000,3090,b000,7000,63,4600
  //   ,249,50a0,e800,3090,50a0,f000,3090,0,4600,246,b100,6000,62,9200
  //   ,4000,28d,b100,6000,63,3060,b901,5010,20,af01,cb06,4000,291,3010
  //   ,bd13,6011,2,d61f,4a00,253,3021,b921,6022,2,9220,4800,253,7000
  //   ,63,bd0c,5010,65,a901,7000,64,60e0,a,50f0,2a4,50d0,200,60c0,b
  //   ,60a0,8,60b0,9,6070,7,6060,6,6050,5,6040,4,6030,3,6020,2,6010
  //   ,1,6000,0,1000,5000,600d,4600,240,b100,6000,20a,9200,4000,2a0
  //   ,50a0,f000,5090,1111,0,5090,2,4600,249,5000,dead,4600,240,7000
  //   ,2ec,b100,6000,64,7010,1,b110,6011,2ec,7010,0,7020,2,7030,3,7040
  //   ,4,7050,5,7060,6,7070,7,70b0,9,70e0,a,70a0,8,b1b0,5000,700,a10a
  //   ,b508,db04,4000,249,db05,4000,614,db06,4000,5dc,db07,4000,5dc
  //   ,db01,4000,41e,db03,4000,425,db00,4000,42d,db02,4800,2e8,b100
  //   ,6000,64,5010,ff03,7010,6,4600,249,5000,ff01,4600,240,0,b100,6000
  //   ,64,60b0,9,60a0,8,6070,7,6060,6,6050,5,6040,4,6030,3,6020,2,6010
  //   ,1,6000,0,1000,9210,4000,30e,7090,0,b901,9b11,4800,308,3087,b110
  //   ,6031,1e5,5040,10,3051,af54,c635,4200,332,5020,1,3051,a952,cb20
  //   ,4000,341,cf54,4800,328,3065,ae64,bf64,6036,1e5,3065,af64,c636
  //   ,4200,331,b951,b921,4600,31d,3015,b911,5050,40,cb51,4100,343,cf14
  //   ,4800,314,3051,ae54,6035,1e5,4600,314,3061,3087,b060,3087,b120
  //   ,6022,20b,7022,35b,4600,353,b120,6022,20c,7022,35b,4600,353,5020
  //   ,10,3030,ae32,6053,1e5,3040,af42,f000,b941,9b11,4000,36b,8f42
  //   ,4800,35b,7053,1e5,b931,bf34,6053,1e5,4600,35b,7053,1e5,3087,bbb1
  //   ,70ab,0,b010,b911,3021,bd23,6032,2,d63f,4200,372,b130,b63f,7032
  //   ,2,b130,b921,7032,2,b921,7032,2,6033,62,b931,7033,62,3021,bd2c
  //   ,5030,65,a923,b130,7032,0,7032,1,7032,2,7032,3,7032,4,7032,5,7032
  //   ,6,7032,7,7032,a,7032,9,603b,0,7032,8,7002,b,3001,3060,b9b1,4600
  //   ,3af,9200,4000,3e3,3010,bd13,6021,2,5030,3e0,a033,a123,5030,7c00
  //   ,a033,a123,b130,6033,63,3043,b44a,a224,7021,2,bd33,6023,2,5010
  //   ,1f,8112,4800,3d2,a220,7023,2,3087,bd13,6021,2,5030,3e0,8132,4000
  //   ,3de,b535,3013,4600,3d2,3030,b435,a223,7021,2,3087,9200,4000,41d
  //   ,3050,bd53,6055,2,5020,7c00,a125,b52a,bd23,6032,2,5040,1f,a143
  //   ,cb40,4800,404,5040,1f,a044,a134,5040,3e0,a145,b545,a234,7032
  //   ,2,3087,5020,1f,a123,bd23,6032,2,5040,3e0,a143,b545,cb40,4000
  //   ,414,3024,4600,406,5040,3e0,a154,b555,a044,a134,a235,7032,2,3087
  //   ,50a0,f000,5090,1000,0,4600,2ed,b100,b110,3078,b974,4600,435,4600
  //   ,249,5000,209,3078,b974,4600,52b,4600,2ed,bbb3,700b,0,707b,1,3020
  //   ,bd23,6022,2,702b,2,9210,4000,44e,5030,3e0,8123,4000,452,b525
  //   ,3002,5070,452,4600,435,3078,b974,4600,3e4,600b,0,3010,bd13,b911
  //   ,6021,2,9220,4000,48e,5030,1e9,cb23,4100,46c,5030,20a,cb23,4900
  //   ,46c,b130,6033,20a,bb31,7033,20a,b911,6011,2,6032,0,b931,7032
  //   ,0,b030,b931,5040,20,cb34,4000,48e,3043,bd43,b941,6054,2,cb52
  //   ,4800,475,b941,6054,2,cb51,4900,475,b951,7054,2,4600,475,3020
  //   ,bd2c,b92b,6022,65,9200,4000,4a3,603b,2,5010,7c00,a131,b53a,bd3c
  //   ,b93b,6033,65,cb23,4000,4b2,3012,5030,400,ae13,5000,ff,a102,b408
  //   ,ae03,3078,b974,4600,34c,600b,0,602b,2,5030,1f,8123,4000,4c1,3002
  //   ,b010,3078,b974,4600,435,600b,0,601b,2,b71f,bd03,7010,2,b110,6011
  //   ,62,bb11,7011,62,607b,1,b9b3,3087,6020,0,bb21,7020,0,9220,4900
  //   ,4f4,3031,bd33,b931,7003,2,b931,7023,2,5020,1e9,cb02,4100,4f1
  //   ,5020,20a,cb02,4900,4f1,b120,6022,20a,b921,7022,20a,5060,1,3087
  //   ,5060,0,3087,6010,0,b911,7010,0,b010,5020,20,b911,cb12,4000,52a
  //   ,3031,bd33,b931,6043,2,cb40,4800,4ff,b931,6043,2,b941,7043,2,9240
  //   ,4100,4ff,bb31,b140,7043,2,5040,1e9,cb04,4100,528,5040,20a,cb04
  //   ,4900,528,b140,6044,20a,bb41,7044,20a,4600,4ff,3087,b010,b120
  //   ,b911,5030,20,cb13,4000,544,3031,bd33,b931,6043,2,cb40,4800,52d
  //   ,b140,7043,2,b931,7043,2,b921,4600,52d,6010,0,a912,7010,0,3087
  //   ,bbb2,707b,0,bd02,b110,b6ad,3091,b7ad,3019,cb01,4900,561,b6ad
  //   ,3090,b7ad,3009,9290,4000,561,700b,1,4600,56a,b160,b9b2,3087,bbb2
  //   ,707b,0,b100,700b,1,b6ad,3090,b7ad,3009,5010,400,ae01,b902,3078
  //   ,b974,4600,30f,d961,4200,594,3010,3006,5020,400,ad62,b568,3031
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  //   contents of Root_Drive (hex, n*v repeats v):
  //   16,4600,2,5000,0,50a0,800,b120,5010,1,2000,b911,2000,5000,3,50a0
  //   ,9000,2000,4d00,10,5000,2,2000
  //   contents of Program_Files (hex, n*v repeats v):
  //   8,4,1f,4,3f,4,51,0,16,4600,2,5000,0,50a0,800,b120,5010,1,2000
  //   ,b911,2000,5000,3,50a0,9000,2000,4d00,10,5000,2,2000,1f,4600,2
  //   ,5010,24,5000,3,50a0,4800,4500,d,2000,4d00,a,3029,cb21,4000,19
  //   ,50a0,8800,3092,2000,4c00,14,4600,6,50a0,9000,3092,2000,4600,1c
  //   ,11,4600,2,5000,3,50a0,8800,4500,b,2000,4d00,8,3019,50a0,4800
  //   ,3091,4600,4
  //   Currently running: Multiprogramming Test
endmodule
